# Fritzing sketch HeliosWatchDiagram (saved by Fritzing 0.8.7b)

parts:
  Part1 = Arduino Pro Mini v13
  Part2 = FTDI Basic Programmer
  CHARGER1 = USB_LiIon_LiPoly_Charger_v1.2
  OLED2 = 128x64 Monochrom OLED Display with SPI Control
  MOTOR1 = Vibration Motor
  R1 = Resistor [tolerance=±5% resistance=10k package=THT]
  S2 = Pushbutton [package=THT]
  U1 = LIPO-110mAh [package=lipo-110]
  Part3 = Bluetooth Module Breakout - Roving Networks (RN-41)

nets:
  N1: Part1.DTR, Part1.D0/TX, Part2.DTR, Part2.RXI
  N2: Part1.D1/RX, Part2.TXO
  VCC: Part1.VCC, OLED2.Vin, Part3.VCC
  GND: Part1.GND, CHARGER1.load_minus_1, OLED2.GND, MOTOR1.NEG, S2.leg1, Part3.GND
  N3: Part1.A4, OLED2.Data
  N4: Part1.A5, OLED2.Clock
  N5: Part1.RAW, CHARGER1.load_plus_1, R1.Pin_1
  N6: Part1.D10_PWM/SS, MOTOR1.POS
  N7: Part1.D5_PWM, R1.Pin_0, S2.leg0
  N8: Part1.D3_PWM, Part3.PIO3, Part3.UARTRX
  N9: Part1.D2, Part3.UARTTX
  N10: Part2.POWER, CHARGER1.dcin_plus_1
  N11: Part2.GND, CHARGER1.dcin_minus_1
  N12: CHARGER1.batt_minus_1, U1.-
  N13: CHARGER1.batt_plus_1, U1.+

custom parts:
  Vibration Motor: An eccentric vibration motor!
